// Logisim project waiting_room.circ as structural Verilog: 1 circuit, main circuit waiting_room
module waiting_room (
  input  IN,
  input  OUT,
  input  Ent,
  input  T,
  input  Clk,
  input  Clr,
  output Open,
  output Close,
  output Q0,
  output Q1,
  output Q2,
  output Q3
);

  wire D0, D1, D2, D3, E0, ENABLE, NCLR, not_2_out, not_3_out, Q0_t, Q1_t, Q2_t, Q3_t, TOGGLE2, TOGGLE3,
       xor_1_out, xor_2_out, xor_3_out;

  xor u_ENABLE (ENABLE, IN, OUT);
  not u_NCLR (NCLR, Clr);
  Register #(.width(1), .trigger("rising")) register_1 (.D(D0), .en(ENABLE), .clk(Clk), .Q(Q0_t), .clr(NCLR));
  Register #(.width(1), .trigger("rising")) register_2 (.D(D1), .en(ENABLE), .clk(Clk), .Q(Q1_t), .clr(NCLR));
  Register #(.width(1), .trigger("rising")) register_3 (.D(D2), .en(ENABLE), .clk(Clk), .Q(Q2_t), .clr(NCLR));
  Register #(.width(1), .trigger("rising")) register_4 (.D(D3), .en(ENABLE), .clk(Clk), .Q(Q3_t), .clr(NCLR));
  xor xor_1 (xor_1_out, Q0_t, IN);
  xor xor_2 (xor_2_out, Q1_t, IN);
  xor xor_3 (xor_3_out, Q2_t, IN);
  not not_1 (E0, xor_1_out);
  not not_2 (not_2_out, xor_2_out);
  not not_3 (not_3_out, xor_3_out);
  and and_1 (TOGGLE2, E0, not_2_out);
  and and_2 (TOGGLE3, TOGGLE2, not_3_out);
  not not_4 (D0, Q0_t);
  xor xor_4 (D1, Q1_t, E0);
  xor xor_5 (D2, Q2_t, TOGGLE2);
  xor xor_6 (D3, Q3_t, TOGGLE3);
  // AND_Gate and_3 is placed but not wired

  // Other names for the same wires on the sheet: U = IN
endmodule
